# Fritzing sketch ticket_game (saved by Fritzing 1.0.1rc)
breadboards: 1

parts:
  Mod1 = Raspberry Pi Pico
  D1 = Diode [package=diode-1n4001]
  S1 = Round Pushbutton
  Part1 = Thermal Printer
  J1 = Camdenboss CTB0158-2 [part_number=CTB0158-2 package=THT]

nets:
  N1: Mod1.pin_1, Part1.RXD
  N2: Mod1.pin_2, Part1.TXD
  N3: Mod1.pin_3, Mod1.pin_8, Mod1.pin_13, Mod1.pin_18, Mod1.pin_23, Mod1.pin_28, Mod1.pin_33, Mod1.pin_38, S1.leg0, Part1.GND, J1.pin2
  N4: Mod1.pin_4, S1.leg1
  N5: Mod1.pin_39, D1.C
  N6: D1.A, Part1.VH, J1.pin1

notes:
  5V @ 4A
  Note this is 3.3v, not used in this project

custom parts:
  Raspberry Pi Pico: Raspberry Pi Pico. Based around the RP2040 microcontroller the Pico is a low cost microcontroller device bringing Raspberry Pi quality, cost, and easy of use to the microcontroller space. Jan 2021, Split part in to two versions: tht (this one) and SMD. This one will drill holes for a .1 in header in pcb to allow plugging in the module as well as providing pads to solder the module to the top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
